// Logisim project Logisim.circ as structural Verilog
module main (
);

  wire clock_1_out, instructiondecoder_1_jmp, instructiondecoder_1_writereg, jump_1_dojump,
       memoryinstruction_1_writereg, memoryinstruction_1_writevalue, or_1_out;
  wire [15:0] alu_1_result, instructiondecoder_1_outval, jump_1_dest, memoryinstruction_1_address,
       memoryinstruction_1_outputval, programcounter_1_instructionpointer, ram_1_dout, registers_1_out1,
       registers_1_out2, registers_1_out3;
  wire [31:0] rom_1_data;

  ROM #(.addrWidth(16), .dataWidth(32)) rom_1 (.addr(programcounter_1_instructionpointer), .data(rom_1_data));
  ProgramCounter programcounter_1 (
    .InstructionPointer(programcounter_1_instructionpointer), .JmpAddres(instructiondecoder_1_outval),
    .Jmp(instructiondecoder_1_jmp), .Clock(clock_1_out));
  RAM #(.addrWidth(16), .asyncread("true"), .dataWidth(16)) ram_1 (
    .addr(memoryinstruction_1_address), .we(memoryinstruction_1_writevalue), .oe(1'b1), .clk(clock_1_out),
    .dout(ram_1_dout));  // open: din
  TopHat tophat_1 ();
  StanApproved stanapproved_1 ();
  Registers registers_1 (
    .Out1(registers_1_out1), .Out2(registers_1_out2), .Out3(registers_1_out3), .Addr1(rom_1_data[23:16]),
    .Addr2(rom_1_data[15:8]), .Addr3(rom_1_data[7:0]), .Clock(clock_1_out),
    .InValue(instructiondecoder_1_outval), .WriteEnabled(or_1_out));
  Clock clock_1 (.out(clock_1_out));
  ALU alu_1 (.Result(alu_1_result), .OpCode(rom_1_data[31:24]), .Value1(registers_1_out1), .Value2(registers_1_out2));
  Jump jump_1 (
    .Dest(jump_1_dest), .DoJump(jump_1_dojump), .Register2(registers_1_out2), .Register3(registers_1_out3),
    .OpCode(rom_1_data[31:24]), .Address({rom_1_data[15:8], rom_1_data[23:16]}), .AddressReg(registers_1_out1));
  MemoryInstruction memoryinstruction_1 (
    .Address(memoryinstruction_1_address), .OutputVal(memoryinstruction_1_outputval),
    .WriteReg(memoryinstruction_1_writereg), .WriteValue(memoryinstruction_1_writevalue),
    .RamValue(ram_1_dout), .OpCode(rom_1_data[31:24]), .Byte1(rom_1_data[23:16]), .Byte2(rom_1_data[15:8]),
    .Byte3(rom_1_data[7:0]), .Reg1(registers_1_out1), .Reg2(registers_1_out2), .Reg3(registers_1_out3));
  or or_1 (or_1_out, instructiondecoder_1_writereg, memoryinstruction_1_writereg);
  InstructionDecoder instructiondecoder_1 (
    .WriteReg(instructiondecoder_1_writereg), .Jmp(instructiondecoder_1_jmp),
    .OutVal(instructiondecoder_1_outval), .OpCode(rom_1_data[31:24]), .JmpValue(jump_1_dest),
    .ALUval(alu_1_result), .DoJump(jump_1_dojump), .MemVal(memoryinstruction_1_outputval));

  // Notes on the sheet:
  //   contents of rom_1 (hex, n*v repeats v):
  //   256*0 fffffff7 ffffffa5 59 ffffffb0 fffffff3 ffffffdb ffffffbe 32 ffffff9f ffffffa4 3e ffffff9a
  //   ffffffb9 ffffffe4 55 22 ffffff97 ffffffd2 73 ffffffab 6c ffffffee ffffffde ffffffd0 ffffffc9 32
  //   ffffffd6 38 67 ffffff87 fffffff9 2c 23 7a ffffffe8 69 49 2f 2b 36 14 ffffff95 51 ffffffb7 75
  //   ffffffdb 5b ffffff83 13 22 5a 75 ffffff93 73 57 ffffffbf 18 fffffff2 72 44 d 54 4d 25 21 ffffff8d
  //   ffffffaa ffffff9c ffffff93 ffffffce 52 9 ffffffaf ffffffae 38 4a ffffff97 ffffffa6 ffffffde 4f 46
  //   ffffffc3 fffffff8 ffffffec ffffffd2 ffffff96 4e fffffff1 fffffff1 6e ffffffe6 77 ffffffbd ffffffc9
  //   61 7c ffffffbb 6 ffffffa5 ffffffb2 19 5f ffffffbc ffffff93 36 17 fffffffb ffffffb8 68 ffffffef 66 6b
  //   fffffff8 ffffffde 53 7a 71 0 4c 4e 1a ffffffcd 39 3b ffffffc0 ffffff8e ffffffbe 18 ffffffb8 d
  //   ffffffe2 12 23 ffffff8c fffffff0 ffffffbd 73 fffffff7 ffffffa1 6b 2e 5c 7a ffffffc1 fffffff2
  //   ffffff9a 73 ffffff86 ffffffb8 58 ffffffd9 ffffffbe 5c 39 74 fffffff7 5c 4d ffffffec ffffffe2
  //   ffffffdf ffffffca 68 24 fffffff9 fffffffb 77 6e 2d 77 33 ffffffca 32 ffffff96 ffffffa3 38 fffffffa
  //   21 61 79 ffffffef 48 7c 2a 7f ffffffd8 ffffff9f 13 ffffffda ffffffad 72 ffffffc0 fffffffa 64 40 51
  //   ffffffe3 55 ffffffd9 ffffff8e 2c ffffffc0 ffffffb9 3e ffffffbd 45 69 ffffffb8 ffffffd9 ffffff99 24
  //   ffffffba 5e 76 ffffffbe 79 4b ffffffd3 ffffffc1 fffffff8 ffffff83 55 ffffffd9 ffffff9c ffffffd0 4 71
  //   0 2a 41 ffffff9d 6 38 fffffff7 3a 2e 16 11 53 2a 58 2b ffffffc6 ffffffb1 4e ffffff8b 26 ffffff93
  //   ffffff89 52 ffffffe3 d ffffff9e ffffffee ffffffa8 5e 29 ffffffd2 4 ffffff99 14 69 4b ffffffbd 18 47
  //   ffffffbe 2 ffffff84 ffffffa1 ffffffe9 75 3d ffffffff 4c ffffffc6 5 2f 3d 60 ffffffff 7c c ffffffba
  //   72 20 68 ffffffec ffffffcd fffffff6 0 ffffff85 ffffffea 73 6d ffffff9b ffffff96 ffffffd7 4e 22 51
  //   ffffff9f ffffffb4 ffffff81 51 3d ffffffc0 62 ffffffcd a ffffff8b ffffffc9 77 7b 45 68 49 ffffff93
  //   ffffffa0 30 ffffff84 ffffff98 6e 2b fffffff5 9 ffffff88 ffffff88 7a ffffffce fffffff2 fffffff7
  //   ffffffc4 ffffffb1 3c 37 5d c 2a ffffffec ffffffec ffffffc4 ffffff97 ffffffb5 ffffffb7 75 ffffff95 7e
  //   6a ffffffee ffffffd9 12 16 ffffffdf 56 fffffff3 7b ffffffd1 27 6d ffffff8a 55 ffffffb1 ffffffe8 24
  //   ffffff80 8 7e 28 ffffff96 ffffff92 ffffffcd ffffffac 4 ffffffe9 d ffffff89 ffffff93 5 64 1d ffffffda
  //   ffffff9a 78 4b fffffff4 ffffffbf 46 ffffffc6 73 ffffffd0 32 ffffff8f ffffff94 ffffff94 5e ffffffbb
  //   ffffffb3 ffffffa1 3e 79 1 fffffffe 6b 53 73 a ffffffb8 ffffffb4 fffffffd ffffff9d ffffff83 ffffffa9
  //   0 6c 4c ffffffeb 0 ffffffb1 ffffff8b 1d ffffff99 b ffffffbd 51 ffffffb3 ffffffa2 ffffffbf ffffffd0
  //   fffffff4 ffffff8e 60 1a 76 79 31 2b ffffffb9 ffffff82 ffffff9e 0 ffffffdb 64 41 58 6 ffffffd7 75
  //   ffffffbf 28 36 2a ffffffc7 ffffffe9 61 fffffff8 ffffff98 ffffffda ffffffe4 75 ffffffab ffffffe9 58
  //   ffffffcb ffffffd2 1d 9 ffffff84 7b 7e ffffffd8 ffffffa7 34 54 63 9 71 ffffff94 62 ffffffdc ffffff8d
  //   ffffff97 54 ffffff8b e d 5a ffffffca 2d 30 61 ffffffe8 ffffff94 3c ffffff87 67 69 1d ffffffb7
  //   ffffffce ffffff8b 6a ffffff95 ffffffbc 1a ffffff92 ffffffa1 40 3d 54 ffffff96 68 1e 74 13 17 39
  //   ffffffab 7d 1b ffffffd6 ffffffde 22 7e ffffffd3 ffffff93 ffffffa2 1c ffffffa7 ffffffa0 ffffff8a 76
  //   ffffffa3 24 41 ffffffc4 79 ffffffbb 27 50 2 ffffffec fffffffa 1 3b ffffffe6 7c 35 ffffff90 6c 52
  //   ffffffd4 5d c 2f ffffffa1 ffffffb1 ffffff96 31 ffffffd3 54 ffffffcc ffffff8a ffffffe4 a 56 63
  //   ffffffa8 19 fffffff8 fffffffc ffffffa0 9 6 17 ffffff8f ffffffaa 16 ffffff96 4e 5b fffffff7 63
  //   ffffffdc ffffff88 ffffffe2 ffffff8f ffffffb9 74 ffffffef ffffffbd 73 38 ffffffca ffffffc1 ffffff80 a
  //   ffffffa6 ffffff83 4e ffffffc2 70 29 ffffff98 ffffff9a 48 75 fffffffb 35 2c 6a ffffffc9 ffffffe2
  //   fffffff6 35 1b 21 ffffff88 4b 2c 65 44 ffffffce ffffffe5 1b ffffffc2 34 ffffffb3 ffffffeb ffffffbc
  //   2a ffffffa0 3d 4d ffffffb5 ffffffa1 fffffffe 5a ffffff9b 2c ffffffa3 50 0 e 6d f 53 7a ffffffee 25
  //   6a 64 ffffffcc 3f ffffffeb f ffffffc5 ffffffdb ffffffee ffffffe5 fffffff3 42 ffffffe0 ffffff86 50
  //   ffffffb5 ffffffaa 22 7b ffffffe6 11 b ffffffbb ffffffa9 5f ffffff85 44 ffffffeb 43 ffffffe0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
endmodule

module HalfAdder (
  input  In1,
  input  In2,
  output Carry,
  output Out1
);

  wire or_1_out;

  or or_1 (or_1_out, In1, In2);
  and and_1 (Carry, In2, In1);
  xor xor_1 (Out1, Carry, or_1_out);
endmodule

module FullAdder (
  input  In1,
  input  In2,
  input  CarryIn,
  output Carry,
  output Result
);

  wire and_1_out, halfadder_1_carry, halfadder_1_out1;

  HalfAdder halfadder_1 (.Carry(halfadder_1_carry), .Out1(halfadder_1_out1), .In1(In1), .In2(In2));
  xor xor_1 (Result, CarryIn, halfadder_1_out1);
  or or_1 (Carry, halfadder_1_carry, and_1_out);
  and and_1 (and_1_out, halfadder_1_out1, CarryIn);
endmodule

module EightBitAdder (
  input  CarryIn,
  input  [7:0] in_2,
  input  [7:0] in_3,
  output [7:0] out_4,
  output CarryOut
);

  wire fulladder_1_carry, fulladder_2_carry, fulladder_3_carry, fulladder_4_carry, fulladder_5_carry,
       fulladder_6_carry, fulladder_7_carry;

  FullAdder fulladder_1 (.In1(in_2[0]), .In2(in_3[0]), .CarryIn(CarryIn), .Carry(fulladder_1_carry), .Result(out_4[0]));
  FullAdder fulladder_2 (
    .In1(in_2[1]), .In2(in_3[1]), .CarryIn(fulladder_1_carry), .Carry(fulladder_2_carry), .Result(out_4[1]));
  FullAdder fulladder_3 (
    .In1(in_2[2]), .In2(in_3[2]), .CarryIn(fulladder_2_carry), .Carry(fulladder_3_carry), .Result(out_4[2]));
  FullAdder fulladder_4 (
    .In1(in_2[3]), .In2(in_3[3]), .CarryIn(fulladder_3_carry), .Carry(fulladder_4_carry), .Result(out_4[3]));
  FullAdder fulladder_5 (
    .In1(in_2[4]), .In2(in_3[4]), .CarryIn(fulladder_4_carry), .Carry(fulladder_5_carry), .Result(out_4[4]));
  FullAdder fulladder_6 (
    .In1(in_2[5]), .In2(in_3[5]), .CarryIn(fulladder_5_carry), .Carry(fulladder_6_carry), .Result(out_4[5]));
  FullAdder fulladder_7 (
    .In1(in_2[6]), .In2(in_3[6]), .CarryIn(fulladder_6_carry), .Carry(fulladder_7_carry), .Result(out_4[6]));
  FullAdder fulladder_8 (
    .In1(in_2[7]), .In2(in_3[7]), .CarryIn(fulladder_7_carry), .Carry(CarryOut), .Result(out_4[7]));
endmodule

module LogicGateDeriving (
  input  in_1,
  input  in_2,
  input  in_3,
  input  in_4,
  input  in_5,
  input  in_6,
  input  in_7,
  input  in_8,
  input  in_9,
  input  in_10,
  input  in_11,
  input  in_12,
  input  in_13,
  output out_14,
  output out_15,
  output out_16,
  output out_17,
  output out_18,
  output out_19,
  output out_20
);

  wire nand_2_out, nand_3_out, nand_4_out, nand_5_out, not_3_out, not_5_out, not_6_out, or_1_out, or_2_out,
       xor_1_out;

  or or_1 (or_1_out, in_8, in_9);
  nand nand_1 (out_14, in_1, in_1);
  nand nand_2 (nand_2_out, in_2, in_3);
  nand nand_3 (nand_3_out, in_4, in_6);
  not not_1 (out_18, or_1_out);
  nand nand_4 (nand_4_out, in_10, in_11);
  or or_2 (or_2_out, in_10, in_11);
  xor xor_1 (xor_1_out, in_12, in_13);
  not not_2 (out_15, nand_2_out);
  not not_3 (not_3_out, in_4);
  nand nand_5 (nand_5_out, nand_3_out, in_6);
  not not_4 (out_20, xor_1_out);
  and and_1 (out_19, nand_4_out, or_2_out);
  nand nand_6 (out_16, not_3_out, nand_5_out);
  not not_5 (not_5_out, in_5);
  not not_6 (not_6_out, in_7);
  nand nand_7 (out_17, not_5_out, not_6_out);
endmodule

module MyMultiplexer (
  input  Input1,
  input  Input2,
  input  Selecter,
  output Output1
);

  wire and_1_out, and_2_out;

  and and_1 (and_1_out, ~Selecter, Input1);  // AND_Gate
  and and_2 (and_2_out, Input2, Selecter);
  xor xor_1 (Output1, and_1_out, and_2_out);
endmodule

module FourBitMultiplexer (
  input  Input0,
  input  Input1,
  input  Input2,
  input  Input3,
  input  [1:0] Selecter,
  output Output1
);

  wire mymultiplexer_1_output1, mymultiplexer_2_output1;

  J_K_Flip_Flop j_k_ff_1 ();  // open: J, clk, K, Q, Qn, preset, reset
  MyMultiplexer mymultiplexer_1 (
    .Output1(mymultiplexer_1_output1), .Input1(Input0), .Input2(Input1), .Selecter(Selecter[0]));
  MyMultiplexer mymultiplexer_2 (
    .Output1(mymultiplexer_2_output1), .Input1(Input2), .Input2(Input3), .Selecter(Selecter[0]));
  MyMultiplexer mymultiplexer_3 (
    .Output1(Output1), .Input1(mymultiplexer_1_output1), .Input2(mymultiplexer_2_output1),
    .Selecter(Selecter[1]));
endmodule

module MyDemultiplexer (
  input  Input1,
  input  Selecter,
  output Output0,
  output Output1
);

  and and_1 (Output0, ~Selecter, Input1);  // AND_Gate
  and and_2 (Output1, Input1, Selecter);
endmodule

module ALU (
  input  [7:0] OpCode,
  input  [15:0] Value1,
  input  [15:0] Value2,
  output [15:0] Result
);

  wire comparator_1_eq, comparator_2_eq, comparator_3_eq, comparator_3_gt, comparator_4_eq, comparator_4_lt,
       comparator_5_gt, comparator_6_lt, not_2_out, or_2_out, or_3_out;
  wire [15:0] adder_1_out, and_1_out, divider_1_out, divider_2_rem, multiplexer_1_out, multiplexer_3_out,
       multiplier_1_out, not_1_out, onebitto16bit_1_bit16, onebitto16bit_2_bit16, onebitto16bit_3_bit16,
       onebitto16bit_4_bit16, onebitto16bit_5_bit16, onebitto16bit_6_bit16, or_1_out, subtractor_1_out,
       xor_1_out;

  Adder #(.width(16)) adder_1 (.a(Value1), .b(Value2), .out(adder_1_out));  // open: cin, cout
  Subtractor #(.width(16)) subtractor_1 (.a(Value1), .b(Value2), .out(subtractor_1_out));  // open: bin, bout
  Multiplier #(.width(16)) multiplier_1 (.a(Value1), .b(Value2), .out(multiplier_1_out));  // open: cin, cout
  Multiplexer #(.enable("false"), .select(3), .width(16)) multiplexer_1 (
    .in0(adder_1_out), .in1(subtractor_1_out), .in2(multiplier_1_out), .in3(divider_1_out),
    .in4(divider_2_rem), .out(multiplexer_1_out), .sel(OpCode[2:0]));  // open: in5, in6, in7
  Divider #(.width(16)) divider_1 (.a(Value1), .b(Value2), .out(divider_1_out));  // open: upper, rem
  Divider #(.width(16)) divider_2 (.a(Value1), .b(Value2), .rem(divider_2_rem));  // open: out, upper
  assign not_1_out = ~Value1;  // NOT_Gate not_1, 16 bits wide
  assign and_1_out = Value1 & Value1;  // AND_Gate and_1, 16 bits wide
  Multiplexer #(.enable("false"), .width(16)) multiplexer_2 (
    .in0(multiplexer_3_out), .in1(multiplexer_1_out), .out(Result), .sel(OpCode[4]));
  assign or_1_out = Value1 | Value1;  // OR_Gate or_1, 16 bits wide
  assign xor_1_out = Value1 ^ Value1;  // XOR_Gate xor_1, 16 bits wide
  Comparator #(.width(16)) comparator_1 (.a(Value1), .b(Value2), .eq(comparator_1_eq));  // open: gt, lt
  Comparator #(.width(16)) comparator_2 (.a(Value1), .b(Value2), .eq(comparator_2_eq));  // open: gt, lt
  not not_2 (not_2_out, comparator_2_eq);
  OneBitTo16Bit onebitto16bit_1 (.Bit16(onebitto16bit_1_bit16), .Bit(comparator_1_eq));
  OneBitTo16Bit onebitto16bit_2 (.Bit16(onebitto16bit_2_bit16), .Bit(not_2_out));
  OneBitTo16Bit onebitto16bit_3 (.Bit16(onebitto16bit_3_bit16), .Bit(or_2_out));
  OneBitTo16Bit onebitto16bit_4 (.Bit16(onebitto16bit_4_bit16), .Bit(or_3_out));
  OneBitTo16Bit onebitto16bit_5 (.Bit16(onebitto16bit_5_bit16), .Bit(comparator_5_gt));
  Multiplexer #(.enable("false"), .select(4), .width(16)) multiplexer_3 (
    .in5(not_1_out), .in6(and_1_out), .in7(or_1_out), .in8(xor_1_out), .in9(onebitto16bit_1_bit16),
    .in10(onebitto16bit_2_bit16), .in11(onebitto16bit_3_bit16), .in12(onebitto16bit_4_bit16),
    .in13(onebitto16bit_5_bit16), .in14(onebitto16bit_6_bit16), .out(multiplexer_3_out), .sel(OpCode[3:0]));  // open: in0, in1, in2, in3, in4, in15
  Comparator #(.width(16)) comparator_3 (
    .a(Value1), .b(Value2), .gt(comparator_3_gt), .eq(comparator_3_eq));  // open: lt
  or or_2 (or_2_out, comparator_3_eq, comparator_3_gt);
  OneBitTo16Bit onebitto16bit_6 (.Bit16(onebitto16bit_6_bit16), .Bit(comparator_6_lt));
  Comparator #(.width(16)) comparator_4 (
    .a(Value1), .b(Value2), .eq(comparator_4_eq), .lt(comparator_4_lt));  // open: gt
  or or_3 (or_3_out, comparator_4_lt, comparator_4_eq);
  Comparator #(.width(16)) comparator_5 (.a(Value1), .b(Value2), .gt(comparator_5_gt));  // open: eq, lt
  Comparator #(.width(16)) comparator_6 (.a(Value1), .b(Value2), .lt(comparator_6_lt));  // open: gt, eq
endmodule

module OneBitTo16Bit (
  input  Bit,
  output [15:0] Bit16
);


  assign Bit16 = {{15{1'b0}}, Bit};
endmodule

module Registers (
  input  [7:0] Addr1,
  input  [7:0] Addr2,
  input  [7:0] Addr3,
  input  Clock,
  input  [15:0] InValue,
  input  WriteEnabled,
  output [15:0] Out1,
  output [15:0] Out2,
  output [15:0] Out3
);

  wire demultiplexer_1_out0, demultiplexer_1_out1, demultiplexer_1_out2, demultiplexer_1_out3,
       demultiplexer_1_out4, demultiplexer_1_out5, demultiplexer_1_out6, demultiplexer_1_out7;
  wire [2:0] eightbitto3_1_out_2, eightbitto3_2_out_2, eightbitto3_3_out_2;
  wire [15:0] register_1_q, register_2_q, register_3_q, register_4_q, register_5_q, register_6_q,
       register_7_q, register_8_q;

  StanApproved stanapproved_1 ();
  Demultiplexer #(.enable("false"), .select(3)) demultiplexer_1 (
    .out0(demultiplexer_1_out0), .out1(demultiplexer_1_out1), .out2(demultiplexer_1_out2),
    .out3(demultiplexer_1_out3), .out4(demultiplexer_1_out4), .out5(demultiplexer_1_out5),
    .out6(demultiplexer_1_out6), .out7(demultiplexer_1_out7), .in(WriteEnabled), .sel(eightbitto3_1_out_2));
  EightBitTo3 eightbitto3_1 (.out_2(eightbitto3_1_out_2), .in_1(Addr1));
  EightBitTo3 eightbitto3_2 (.out_2(eightbitto3_2_out_2), .in_1(Addr2));
  EightBitTo3 eightbitto3_3 (.out_2(eightbitto3_3_out_2), .in_1(Addr3));
  Register #(.width(16)) register_1 (
    .D(InValue), .en(demultiplexer_1_out0), .Q(register_1_q), .clk(Clock));  // open: clr
  Register #(.width(16)) register_2 (
    .D(InValue), .en(demultiplexer_1_out1), .Q(register_2_q), .clk(Clock));  // open: clr
  Register #(.width(16)) register_3 (
    .D(InValue), .en(demultiplexer_1_out2), .Q(register_3_q), .clk(Clock));  // open: clr
  Register #(.width(16)) register_4 (
    .D(InValue), .en(demultiplexer_1_out3), .Q(register_4_q), .clk(Clock));  // open: clr
  Register #(.width(16)) register_5 (
    .D(InValue), .en(demultiplexer_1_out4), .Q(register_5_q), .clk(Clock));  // open: clr
  Register #(.width(16)) register_6 (
    .D(InValue), .en(demultiplexer_1_out5), .Q(register_6_q), .clk(Clock));  // open: clr
  Register #(.width(16)) register_7 (
    .D(InValue), .en(demultiplexer_1_out6), .Q(register_7_q), .clk(Clock));  // open: clr
  Register #(.width(16)) register_8 (
    .D(InValue), .en(demultiplexer_1_out7), .Q(register_8_q), .clk(Clock));  // open: clr
  Multiplexer #(.enable("false"), .select(3), .width(16)) multiplexer_1 (
    .in0(register_1_q), .in1(register_2_q), .in2(register_3_q), .in3(register_4_q), .in4(register_5_q),
    .in5(register_6_q), .in6(register_7_q), .in7(register_8_q), .out(Out1), .sel(eightbitto3_1_out_2));
  Multiplexer #(.enable("false"), .select(3), .width(16)) multiplexer_2 (
    .in0(register_1_q), .in1(register_2_q), .in2(register_3_q), .in3(register_4_q), .in4(register_5_q),
    .in5(register_6_q), .in6(register_7_q), .in7(register_8_q), .out(Out2), .sel(eightbitto3_2_out_2));
  Multiplexer #(.enable("false"), .select(3), .width(16)) multiplexer_3 (
    .in0(register_1_q), .in1(register_2_q), .in2(register_3_q), .in3(register_4_q), .in4(register_5_q),
    .in5(register_6_q), .in6(register_7_q), .in7(register_8_q), .out(Out3), .sel(eightbitto3_3_out_2));
endmodule

module EightBitTo3 (
  input  [7:0] in_1,
  output [2:0] out_2
);


  assign out_2 = in_1[2:0];
endmodule

module ProgramCounter (
  input  [15:0] JmpAddres,
  input  Jmp,
  input  Clock,
  output [15:0] InstructionPointer
);

  wire [15:0] adder_1_out, multiplexer_1_out;

  Multiplexer #(.enable("false"), .width(16)) multiplexer_1 (
    .in0(adder_1_out), .out(multiplexer_1_out), .sel(Jmp));  // open: in1
  Register #(.width(16)) IP (.D(multiplexer_1_out), .en(1'b1), .Q(InstructionPointer), .clk(Clock));  // open: clr
  Adder #(.width(16)) adder_1 (.a(InstructionPointer), .b(16'h1), .out(adder_1_out));  // open: cin, cout
endmodule

module InstructionDecoder (
  input  [7:0] OpCode,
  input  [15:0] JmpValue,
  input  [15:0] ALUval,
  input  DoJump,
  input  [15:0] MemVal,
  output WriteReg,
  output Jmp,
  output [15:0] OutVal
);

  wire and_1_out, and_2_out, and_3_out, not_1_out;
  wire [15:0] multiplexer_1_out;

  and and_1 (and_1_out, OpCode[4], OpCode[5], OpCode[6]);
  and and_2 (and_2_out, ~OpCode[4], ~OpCode[5], OpCode[6]);  // AND_Gate
  and and_3 (and_3_out, ~OpCode[4], ~OpCode[5], ~OpCode[6]);  // AND_Gate
  Multiplexer #(.enable("false"), .width(16)) multiplexer_1 (
    .in0(ALUval), .in1(JmpValue), .out(multiplexer_1_out), .sel(and_1_out));
  Multiplexer #(.enable("false"), .width(16)) multiplexer_2 (
    .in0(multiplexer_1_out), .in1(MemVal), .out(OutVal), .sel(and_2_out));
  not not_1 (not_1_out, and_1_out);
  and and_4 (WriteReg, not_1_out, ~and_3_out);  // AND_Gate
  and and_5 (Jmp, and_1_out, DoJump);
endmodule

module Jump (
  input  [7:0] OpCode,
  input  [15:0] Address,
  input  [15:0] AddressReg,
  input  [15:0] Register2,
  input  [15:0] Register3,
  output [15:0] Dest,
  output DoJump
);

  Multiplexer #(.enable("false"), .width(16)) multiplexer_1 (
    .in0(Address), .in1(AddressReg), .out(Dest), .sel(OpCode[0]));
  Multiplexer #(.enable("false"), .select(2)) multiplexer_2 (
    .in0(1'b0), .in1(1'b0), .in2(Register3[0]), .in3(Register2[0]), .out(DoJump), .sel(OpCode[1:0]));
endmodule

module MemoryInstruction (
  input  [7:0] OpCode,
  input  [7:0] Byte1,
  input  [7:0] Byte2,
  input  [7:0] Byte3,
  input  [15:0] Reg1,
  input  [15:0] Reg2,
  input  [15:0] Reg3,
  input  [15:0] RamValue,
  output [15:0] Address,
  output [15:0] OutputVal,
  output WriteReg,
  output WriteValue
);

  wire comparator_1_eq;
  wire [2:0] multiplexer_3_out;

  Comparator comparator_1 (.a(OpCode), .b({8{1'b0}}), .eq(comparator_1_eq));  // open: gt, lt
  Multiplexer #(.enable("false"), .select(3), .width(16)) multiplexer_1 (
    .in0(Reg1), .in1(Reg1), .in2({Byte3, Byte2}), .in3(Reg2), .in4({Byte2, Byte1}), .in5(Reg2), .in6(Reg1),
    .in7(Reg1), .out(Address), .sel(OpCode[2:0]));
  Multiplexer #(.enable("false"), .select(3), .width(16)) multiplexer_2 (
    .in0({Byte3, Byte2}), .in1(Reg2), .in2(RamValue), .in3(RamValue), .in4(Reg3), .in5(Reg3),
    .out(OutputVal), .sel(OpCode[2:0]));  // open: in6, in7
  Multiplexer #(.enable("false"), .select(3), .width(3)) multiplexer_3 (
    .in0(3'b001), .in1(3'b001), .in2(3'b001), .in3(3'b001), .in4(3'b010), .in5(3'b010), .in6(3'b010),
    .in7(3'b001), .out({multiplexer_3_out[2], WriteValue, multiplexer_3_out[0]}), .sel(OpCode[2:0]));
  Multiplexer #(.enable("false")) multiplexer_4 (
    .in0(multiplexer_3_out[0]), .in1(1'b0), .out(WriteReg), .sel(comparator_1_eq));
endmodule
